# Fritzing sketch warpdrive-lighting-circuit (saved by Fritzing 0.9.2b)
breadboards: 1

parts:
  Bauteil1 = Arduino Uno (Rev3)
  IC2 = ULN2803A [package=THT]
  +12V = Power Jack [package=power_jack_pth_lock]
  LED1 = smd LED [color="White (6500K)" package="0603 [SMD]"]
  LED2 = smd LED [color="White (6500K)" package="0603 [SMD]"]
  LED3 = smd LED [color="White (6500K)" package="0603 [SMD]"]
  LED4 = smd LED [color="White (6500K)" package="0603 [SMD]"]
  LED5 = smd LED [color="White (6500K)" package="0603 [SMD]"]
  LED6 = smd LED [color="White (6500K)" package="0603 [SMD]"]
  LED7 = smd LED [color="White (6500K)" package="0603 [SMD]"]
  LED8 = smd LED [color="White (6500K)" package="0603 [SMD]"]
  IC1 = ULN2803A [package=THT]
  U1 = POT [package=pot_mammoth]

nets:
  N1: Bauteil1.A3, U1.S
  N2: Bauteil1.D8, IC2.In_7
  N3: Bauteil1.D9_PWM, IC2.In_8
  DIM: Bauteil1.D11_PWM/MOSI, IC1.In_1, IC1.In_2, IC1.In_3, IC1.In_4, IC1.In_5, IC1.In_6, IC1.In_7, IC1.In_8
  GND: Bauteil1.GND, IC2.0V, +12V.GND, IC1.0V, U1.E
  N4: Bauteil1.D2, IC2.In_1
  N5: Bauteil1.D3_PWM, IC2.In_2
  N6: Bauteil1.D4, IC2.In_3
  N7: Bauteil1.D5_PWM, IC2.In_4
  N8: Bauteil1.D6_PWM, IC2.In_5
  N9: Bauteil1.D7, IC2.In_6
  N10: Bauteil1.5V, U1.A
  N11: Bauteil1.VIN, +12V.PWR, LED1.anode, LED2.anode, LED3.anode, LED4.anode, LED5.anode, LED6.anode, LED7.anode, LED8.anode
  N12: IC2.Out_8, LED8.cathode, IC1.Out_1
  N13: IC2.Out_7, LED7.cathode, IC1.Out_2
  N14: IC2.Out_6, LED6.cathode, IC1.Out_3
  N15: IC2.Out_5, LED5.cathode, IC1.Out_4
  N16: IC2.Out_4, LED4.cathode, IC1.Out_5
  N17: IC2.Out_3, LED3.cathode, IC1.Out_6
  N18: IC2.Out_2, LED2.cathode, IC1.Out_7
  N19: IC2.Out_1, LED1.cathode, IC1.Out_8

notes:
  12V DC in
  Each LED represents a 12V LED strip.Do not use single LEDs here or they will burn...
  yellow = +12V
  red = +5V
  blue = pwm signal
  purple = on/off signal
  black = ground / switched ground
  green = analog signal

// code stored in the sketch: WarpDriveLighting.ino
const uint8_t ledPins[] = {2, 3, 4, 5, 6, 7, 8, 9};

const uint8_t ledCount = 8;

const uint8_t fadePin = 11;

const uint8_t controlPin = 3;

const uint8_t frames[] = {B10000001, B01000010, B00100100, B00011000};

const boolean invertControl = true;

uint8_t currentFrame = 0;

void setup()
{
  for(uint8_t i = 0; i < ledCount; i++)
  {
    pinMode(ledPins[i], OUTPUT);
  }
  pinMode(fadePin, OUTPUT);
  pinMode(controlPin, INPUT);
}

void loop()
{
  int controlValue = readControlValue();
  int fadeValue = map(controlValue, 0, 1023, 0, 255);
  analogWrite(fadePin, fadeValue);
  
  if(currentFrame > 3)
  {
    currentFrame = 0;
  }
  for(uint8_t i = 0; i < 8; i++)
  {
    digitalWrite(ledPins[i], LOW);
    digitalWrite(ledPins[i], bitRead(frames[currentFrame], i));
  }
  currentFrame++;
  delay(500);  
}

int readControlValue()
{
  int controlValue = analogRead(controlPin);
  if (invertControl)
  {
    controlValue = 1023 - controlValue;
  }
  return controlValue;
}
